# Fritzing sketch sketch (saved by Fritzing 0.9.6b)
breadboards: 1

parts:
  WeMos_D1_Mini1 = WeMos D1 Mini  # not connected
  U1 = WS2812 RGB LED strip
  U2 = WS2812 RGB LED strip
  WeMos_D1_Mini2 = WeMos D1 Mini  # not connected
  U3 = WS2812 RGB LED strip
  U4 = WS2812 RGB LED strip
  WeMos_D1_Mini3 = WeMos D1 Mini  # not connected
  U5 = WS2812 RGB LED strip
  U6 = WS2812 RGB LED strip

nets:
  GND: U1.GND, U2.GND, U3.GND, U4.GND, U5.GND, U6.GND
  VCC: U1.VCC, U2.VCC, U3.VCC, U4.VCC, U5.VCC, U6.VCC

notes:
  DMA variant
  (recommended, disconnect before flashing)
  UART variant
  Bitbang variant
  (example, not recommended)

custom parts:
  WS2812 RGB LED strip: WS2812 strip
